# Fritzing sketch Untitled Sketch (saved by Fritzing 0.9.3b)
breadboards: 1

parts:
  Componente1 = Arduino Uno (Rev3)
  S1 = Reed switch [package=THT]
  R1 = Resistor [tolerance=±5% resistance=1k package=THT]  # not connected
  R2 = Resistor [tolerance=±5% resistance=330 package=THT]
  LED1 = LED - 5mm [color="Red (633nm)" package="5 mm [THT]"]
  J1 = Piezo Speaker

nets:
  N1: Componente1.D8, J1.pin2
  N2: Componente1.D13/SCK, R2.Pin_0
  N3: Componente1.GND, S1.pin_2, LED1.cathode, J1.pin1
  N4: Componente1.D2, S1.pin_1
  N5: R2.Pin_1, LED1.anode
